# Fritzing sketch VeloPod (saved by Fritzing 1.0.7)
circuit board: 7.76817cm x 6.97495cm

parts:
  XIAO_ESP32S3 = XIAO ESP32S3 [package="DIP (Dual Inline) [THT]"]
  STATUS_LED = LEDs [package=led10mm]
  DISPLAY_MODULE = TFT 2.2 inch 320x240 w microSD [part_number=1480]
  RESISTOR = Resistor [tolerance=±0.05% resistance=220 package="2010 [SMD]"]
  JOYSTICK_CONTROLLER = KY-023 Dual Axis Joystick Module [package="Breakout board"]

nets:
  N1: XIAO_ESP32S3.D0, DISPLAY_MODULE.RESET
  N2: XIAO_ESP32S3.D1, DISPLAY_MODULE.LCDCS
  N3: XIAO_ESP32S3.D2, DISPLAY_MODULE.DC
  N4: XIAO_ESP32S3.D3, DISPLAY_MODULE.SDCS
  N5: XIAO_ESP32S3.D4, JOYSTICK_CONTROLLER.VRx
  N6: XIAO_ESP32S3.D5, JOYSTICK_CONTROLLER.VRy
  N7: XIAO_ESP32S3.D6, JOYSTICK_CONTROLLER.SW
  N8: XIAO_ESP32S3.D7, RESISTOR.Pin_1
  N9: XIAO_ESP32S3.D8, DISPLAY_MODULE.SCLK
  N10: XIAO_ESP32S3.D9, DISPLAY_MODULE.MISO
  N11: XIAO_ESP32S3.D10, DISPLAY_MODULE.MOSI
  GND: XIAO_ESP32S3.GND, STATUS_LED.C, DISPLAY_MODULE.GND, JOYSTICK_CONTROLLER.GND
  5V: XIAO_ESP32S3.5V, DISPLAY_MODULE.VIN, DISPLAY_MODULE.BACKLIGHT, JOYSTICK_CONTROLLER.+5V
  N12: STATUS_LED.A, RESISTOR.Pin_0

custom parts:
  XIAO ESP32S3: Seeed Studio XIAO ESP32S3 leverages 240MHz Xtensa 32-bit LX7 dual-core processor, supporting both WiFi and BLE 5.0 wireless connectivities, a 2.4GHz Rod antenna, allows for deep sleep mode with power consumption as low as 14μA while supporting lithium battery charging management. Ideal for the Internet of Things, Smart Homes, Wireless wearable devices, Robotics, etc.
  TFT 2.2 inch 320x240 w microSD: This lovely little display breakout is the best way to add a small, colorful and bright display to any project. Since the display uses 4-wire SPI to communicate and has its own pixel-addressable frame buffer, it can be used with every kind of microcontroller. Even a very small one with low memory and few pins available! The 2.2" display has 320x240 color pixels.
  KY-023 Dual Axis Joystick Module: KY-023 Dual-Axis Joystick Module.
